# Fritzing sketch DiseñoBalanza (saved by Fritzing 1.0.4)
breadboards: 1

parts:
  Componente2 = Arduino Uno (Rev3)
  S1 = Load Sensor - 50kg [part_number=SEN-10245]
  S2 = Load Sensor - 50kg [part_number=SEN-10245]
  S3 = Load Sensor - 50kg [part_number=SEN-10245]
  S4 = Load Sensor - 50kg [part_number=SEN-10245]
  PART2 = SparkFun Load Cell Amplifier - HX711 [part_number=SEN-13230]
  VCC1 = Battery block 9V [internal_resistance=0.1Ω]  # not connected
  R1 = Resistor [tolerance=±5% resistance=1k package="0805 [SMD]"]
  R2 = Resistor [tolerance=±1% resistance=2.2k package="0805 [SMD]"]
  Componente4 = Bluetooth HM-10

nets:
  N1: Componente2.D10_PWM/SS, Componente4.TXD
  N2: Componente2.D11_PWM/MOSI, R1.Pin_0
  N3: Componente2.D4, PART2.DAT
  N4: Componente2.D5_PWM, PART2.CLK
  VCC: Componente2.5V, PART2.VCC, Componente4.VCC
  GND: Componente2.GND, PART2.GND, R2.Pin_0, Componente4.GND
  N5: S1.B, S2.B
  N6: S1.W, S3.W
  N7: S1.R, PART2.RED
  N8: S2.W, S4.W
  N9: S2.R, PART2.WHT
  N10: S3.B, S4.B
  N11: S3.R, PART2.GRN
  N12: S4.R, PART2.BLK
  N13: R1.Pin_1, R2.Pin_1, Componente4.RXD

custom parts:
  Load Sensor - 50kg: Half-wheatstone bridge Load Cell modified from the Fritzing Repo This load sensor, sometimes called a strain gauge, is the same one found in digital bathroom scales (you know, the ones you use in January for your New Year's resolutions, and then forget about a month later). This sensor can measure up to about 110 pounds.
  SparkFun Load Cell Amplifier - HX711: The SparkFun Load Cell Amplifier is a small breakout board for the HX711 IC that allows you to easily read load cells to measure weight. By connecting the amplifier to your microcontroller you will be able to read the changes in the resistance of the load cell and with some calibration you’ll be able to get very accurate weight measurements. This can be handy for creating your own industrial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
